# Fritzing sketch connections (saved by Fritzing 0.9.4)

parts:
  XIAO_ESP32S1 = XIAO ESP32S3 [package="DIP (Dual Inline) [THT]"]
  LCD1 = TFT 1.8 inch 160x128 w SD
  S1 = Pushbutton [package="[THT]"]

nets:
  N1: XIAO_ESP32S1.D0, LCD1.pin3
  N2: XIAO_ESP32S1.D1, LCD1.pin_5
  N3: XIAO_ESP32S1.D2, LCD1.pin4
  N4: XIAO_ESP32S1.D3, S1.Pin_3, S1.Pin_4
  N5: XIAO_ESP32S1.D4, S1.Pin_1, S1.Pin_2
  N6: XIAO_ESP32S1.D8, LCD1.pin_7
  N7: XIAO_ESP32S1.D10, LCD1.pin_6
  N8: XIAO_ESP32S1.3V3, LCD1.pin_8
  N9: XIAO_ESP32S1.GND, LCD1.pin2
  N10: XIAO_ESP32S1.5V, LCD1.pin_1

custom parts:
  XIAO ESP32S3: Seeed Studio XIAO ESP32S3 leverages 240MHz Xtensa 32-bit LX7 dual-core processor, supporting both WiFi and BLE 5.0 wireless connectivities, a 2.4GHz Rod antenna, allows for deep sleep mode with power consumption as low as 14μA while supporting lithium battery charging management. Ideal for the Internet of Things, Smart Homes, Wireless wearable devices, Robotics, etc.
  TFT 1.8 inch 160x128 w SD: This is a generic 1.8 tft spi lcd display available on ebay and others. The 1.8" display has 128x160 color pixels.
